// Logisim project practica4.circ as structural Verilog: 8 circuits, main circuit ALU_y_Banco_Memoria
module Registro_8_bits (
  input  Reloj,
  input  [7:0] Entrada,
  output [7:0] Salida,
  output nEntrada
);

  wire and_1_out, and_2_out, d_ff_1_qn, d_ff_2_qn, d_ff_3_qn, d_ff_4_qn, d_ff_5_qn, d_ff_6_qn, d_ff_7_qn,
       d_ff_8_qn;

  D_Flip_Flop d_ff_1 (.clk(Reloj), .D(Entrada[0]), .Q(Salida[0]), .Qn(d_ff_1_qn));  // open: preset, en, reset
  D_Flip_Flop d_ff_2 (.clk(Reloj), .D(Entrada[1]), .Q(Salida[1]), .Qn(d_ff_2_qn));  // open: preset, en, reset
  D_Flip_Flop d_ff_3 (.clk(Reloj), .D(Entrada[2]), .Q(Salida[2]), .Qn(d_ff_3_qn));  // open: preset, en, reset
  D_Flip_Flop d_ff_4 (.clk(Reloj), .D(Entrada[3]), .Q(Salida[3]), .Qn(d_ff_4_qn));  // open: preset, en, reset
  D_Flip_Flop d_ff_5 (.clk(Reloj), .D(Entrada[4]), .Q(Salida[4]), .Qn(d_ff_5_qn));  // open: preset, en, reset
  D_Flip_Flop d_ff_6 (.clk(Reloj), .D(Entrada[5]), .Q(Salida[5]), .Qn(d_ff_6_qn));  // open: preset, en, reset
  D_Flip_Flop d_ff_7 (.clk(Reloj), .D(Entrada[6]), .Q(Salida[6]), .Qn(d_ff_7_qn));  // open: preset, en, reset
  D_Flip_Flop d_ff_8 (.clk(Reloj), .D(Entrada[7]), .Q(Salida[7]), .Qn(d_ff_8_qn));  // open: preset, en, reset
  and and_1 (and_1_out, d_ff_1_qn, d_ff_2_qn, d_ff_3_qn, d_ff_4_qn);
  and and_2 (and_2_out, d_ff_5_qn, d_ff_6_qn, d_ff_7_qn, d_ff_8_qn);
  and and_3 (nEntrada, and_1_out, and_2_out);
endmodule

module Banco_Memoria (
  input  [1:0] Leer_dato_1,
  input  [1:0] Leer_dato_2,
  input  [1:0] Escribir_registro,
  input  [7:0] Escribir_Datos,
  input  Escribir,
  output [7:0] Leer_Datos_1,
  output [7:0] Leer_Datos_2
);

  wire demultiplexer_1_out0, demultiplexer_1_out1, demultiplexer_1_out2, demultiplexer_1_out3;
  wire [7:0] demultiplexer_2_out0, demultiplexer_2_out1, demultiplexer_2_out2, demultiplexer_2_out3,
       registro_8_bits_1_salida, registro_8_bits_2_salida, registro_8_bits_3_salida, registro_8_bits_4_salida;

  Demultiplexer #(.select(2), .enable("false")) demultiplexer_1 (
    .out0(demultiplexer_1_out0), .out1(demultiplexer_1_out1), .out2(demultiplexer_1_out2),
    .out3(demultiplexer_1_out3), .in(Escribir), .sel(Escribir_registro));
  Demultiplexer #(.select(2), .width(8), .enable("false")) demultiplexer_2 (
    .out0(demultiplexer_2_out0), .out1(demultiplexer_2_out1), .out2(demultiplexer_2_out2),
    .out3(demultiplexer_2_out3), .in(Escribir_Datos), .sel(Escribir_registro));
  Registro_8_bits registro_8_bits_1 (
    .Reloj(demultiplexer_1_out0), .Entrada(demultiplexer_2_out0), .Salida(registro_8_bits_1_salida));  // open: nEntrada
  Registro_8_bits registro_8_bits_2 (
    .Reloj(demultiplexer_1_out1), .Entrada(demultiplexer_2_out1), .Salida(registro_8_bits_2_salida));  // open: nEntrada
  Registro_8_bits registro_8_bits_3 (
    .Reloj(demultiplexer_1_out2), .Entrada(demultiplexer_2_out2), .Salida(registro_8_bits_3_salida));  // open: nEntrada
  Registro_8_bits registro_8_bits_4 (
    .Reloj(demultiplexer_1_out3), .Entrada(demultiplexer_2_out3), .Salida(registro_8_bits_4_salida));  // open: nEntrada
  Multiplexer #(.select(2), .width(8), .enable("false")) multiplexer_1 (
    .in0(registro_8_bits_1_salida), .in1(registro_8_bits_2_salida), .in2(registro_8_bits_3_salida),
    .in3(registro_8_bits_4_salida), .out(Leer_Datos_1), .sel(Leer_dato_1));
  Multiplexer #(.select(2), .width(8), .enable("false")) multiplexer_2 (
    .in0(registro_8_bits_1_salida), .in1(registro_8_bits_2_salida), .in2(registro_8_bits_3_salida),
    .in3(registro_8_bits_4_salida), .out(Leer_Datos_2), .sel(Leer_dato_2));
endmodule

module ALU_y_Banco_Memoria (
  input  [1:0] Leer_Dato_1,
  input  [1:0] Leer_Dato_2,
  input  [1:0] Escribir_registro,
  input  [7:0] Entrada,
  input  Escribir,
  input  [2:0] \Operación ,
  output Cero,
  output Desborde,
  output Negativo,
  output \_0__Lógica___1__Aritmética ,
  output [7:0] Salida
);

  wire [7:0] Banco_de_Memoria_leer_datos_1, Banco_de_Memoria_leer_datos_2;

  Banco_Memoria Banco_de_Memoria (
    .Leer_dato_1(Leer_Dato_1), .Leer_dato_2(Leer_Dato_2), .Escribir_registro(Escribir_registro),
    .Escribir_Datos(Entrada), .Escribir(Escribir), .Leer_Datos_1(Banco_de_Memoria_leer_datos_1),
    .Leer_Datos_2(Banco_de_Memoria_leer_datos_2));
  ALU ALU (
    .A(Banco_de_Memoria_leer_datos_1), .B(Banco_de_Memoria_leer_datos_2), .\Operación (\Operación ),
    .Cero(Cero), .Desborde(Desborde), .Negativo(Negativo),
    .\_0__Lógica___1__Aritmética (\_0__Lógica___1__Aritmética ), .Resultado(Salida));

  // Notes on the sheet:
  //   000. AND
  //   001. OR
  //   010. ADD
  //   011. SUB
  //   100. NEGATE
  //   111. PASS
  //   101. INCREMENT
  //   110. DECREMENT
endmodule

module Add_1_bit (
  input  Acarreo_de_entrada,
  input  A,
  input  B,
  output Suma,
  output Acarreo_de_Salida
);

  wire and_1_out, and_2_out, xor_1_out;

  xor xor_1 (xor_1_out, A, B);
  and and_1 (and_1_out, A, B);
  and and_2 (and_2_out, Acarreo_de_entrada, xor_1_out);
  xor xor_2 (Suma, Acarreo_de_entrada, xor_1_out);
  xor xor_3 (Acarreo_de_Salida, and_2_out, and_1_out);
endmodule

module Add_8_bits (
  input  Acarreo_de_Entrada,
  input  [7:0] A,
  input  [7:0] B,
  output [7:0] Resultado,
  output out_5
);

  wire add_1_bit_1_acarreo_de_salida, add_1_bit_2_acarreo_de_salida, add_1_bit_3_acarreo_de_salida,
       add_1_bit_4_acarreo_de_salida, add_1_bit_5_acarreo_de_salida, add_1_bit_6_acarreo_de_salida,
       add_1_bit_7_acarreo_de_salida;

  Add_1_bit add_1_bit_1 (
    .Acarreo_de_entrada(Acarreo_de_Entrada), .A(A[0]), .B(B[0]), .Suma(Resultado[0]),
    .Acarreo_de_Salida(add_1_bit_1_acarreo_de_salida));
  Add_1_bit add_1_bit_2 (
    .Acarreo_de_entrada(add_1_bit_1_acarreo_de_salida), .A(A[1]), .B(B[1]), .Suma(Resultado[1]),
    .Acarreo_de_Salida(add_1_bit_2_acarreo_de_salida));
  Add_1_bit add_1_bit_3 (
    .Acarreo_de_entrada(add_1_bit_2_acarreo_de_salida), .A(A[2]), .B(B[2]), .Suma(Resultado[2]),
    .Acarreo_de_Salida(add_1_bit_3_acarreo_de_salida));
  Add_1_bit add_1_bit_4 (
    .Acarreo_de_entrada(add_1_bit_3_acarreo_de_salida), .A(A[3]), .B(B[3]), .Suma(Resultado[3]),
    .Acarreo_de_Salida(add_1_bit_4_acarreo_de_salida));
  Add_1_bit add_1_bit_5 (
    .Acarreo_de_entrada(add_1_bit_4_acarreo_de_salida), .A(A[4]), .B(B[4]), .Suma(Resultado[4]),
    .Acarreo_de_Salida(add_1_bit_5_acarreo_de_salida));
  Add_1_bit add_1_bit_6 (
    .Acarreo_de_entrada(add_1_bit_5_acarreo_de_salida), .A(A[5]), .B(B[5]), .Suma(Resultado[5]),
    .Acarreo_de_Salida(add_1_bit_6_acarreo_de_salida));
  Add_1_bit add_1_bit_7 (
    .Acarreo_de_entrada(add_1_bit_6_acarreo_de_salida), .A(A[6]), .B(B[6]), .Suma(Resultado[6]),
    .Acarreo_de_Salida(add_1_bit_7_acarreo_de_salida));
  Add_1_bit add_1_bit_8 (
    .Acarreo_de_entrada(add_1_bit_7_acarreo_de_salida), .A(A[7]), .B(B[7]), .Suma(Resultado[7]),
    .Acarreo_de_Salida(out_5));
endmodule

module ALU (
  input  [7:0] A,
  input  [7:0] B,
  input  [2:0] \Operación ,
  output Cero,
  output Desborde,
  output Negativo,
  output \_0__Lógica___1__Aritmética ,
  output [7:0] Resultado
);

  wire add_8_bits_1_out_5, add_8_bits_2_out_5, and_2_out, not_2_out, or_3_out, or_5_out;
  wire [7:0] add_8_bits_1_resultado, add_8_bits_2_resultado, and_1_out, not_1_out, or_1_out,
       sub_8_bits_1_resultado, sub_8_bits_2_resultado;

  Add_8_bits add_8_bits_1 (
    .Acarreo_de_Entrada(1'b0), .A(A), .B(B), .Resultado(add_8_bits_1_resultado), .out_5(add_8_bits_1_out_5));
  Sub_8_bits sub_8_bits_1 (.A(A), .B(B), .Resultado(sub_8_bits_1_resultado));  // open: out_4
  Add_8_bits add_8_bits_2 (
    .Acarreo_de_Entrada(1'b0), .A(A), .B(8'h1), .Resultado(add_8_bits_2_resultado), .out_5(add_8_bits_2_out_5));
  Sub_8_bits sub_8_bits_2 (.A(A), .B(8'h1), .Resultado(sub_8_bits_2_resultado));  // open: out_4
  assign and_1_out = A & B;  // AND_Gate and_1, 8 bits wide
  assign or_1_out = A | B;  // OR_Gate or_1, 8 bits wide
  assign not_1_out = ~A;  // NOT_Gate not_1, 8 bits wide
  Multiplexer #(.select(3), .width(8), .enable("false")) multiplexer_1 (
    .in0(and_1_out), .in1(or_1_out), .in2(add_8_bits_1_resultado), .in3(sub_8_bits_1_resultado),
    .in4(not_1_out), .in5(add_8_bits_2_resultado), .in6(sub_8_bits_2_resultado), .in7(A), .out(Resultado),
    .sel(\Operación ));
  or or_2 (Desborde, add_8_bits_1_out_5, add_8_bits_2_out_5);
  not not_2 (not_2_out, \Operación [2]);
  and and_2 (and_2_out, \Operación [0], \Operación [1], not_2_out);
  or or_3 (or_3_out, Resultado[0], Resultado[1], Resultado[2], Resultado[3], Resultado[4]);
  or or_4 (\_0__Lógica___1__Aritmética , \Operación [1], \Operación [2]);
  or or_5 (or_5_out, or_3_out, Resultado[5], Resultado[6], Resultado[7]);
  not not_3 (Cero, or_5_out);
  and and_3 (Negativo, Resultado[7], and_2_out);

  // Notes on the sheet:
  //   000. AND
  //   001. OR
  //   010. ADD
  //   011. SUB
  //   100. NEGATE
  //   101. INCREMENT
  //   110. DECREMENT
  //   111. PASS
endmodule

module Sub_8_bits (
  input  [7:0] A,
  input  [7:0] B,
  output [7:0] Resultado,
  output out_4
);

  wire add_1_bit_1_acarreo_de_salida, add_1_bit_2_acarreo_de_salida, add_1_bit_3_acarreo_de_salida,
       add_1_bit_4_acarreo_de_salida, add_1_bit_5_acarreo_de_salida, add_1_bit_6_acarreo_de_salida,
       add_1_bit_7_acarreo_de_salida, not_1_out, not_2_out, not_3_out, not_4_out, not_5_out, not_6_out,
       not_7_out;

  not not_1 (not_1_out, B[0]);
  not not_2 (not_2_out, B[1]);
  not not_3 (not_3_out, B[3]);
  not not_4 (not_4_out, B[4]);
  not not_5 (not_5_out, B[5]);
  not not_6 (not_6_out, B[6]);
  not not_7 (not_7_out, B[7]);
  Add_1_bit add_1_bit_1 (
    .Acarreo_de_entrada(1'b1), .A(A[0]), .B(not_1_out), .Suma(Resultado[0]),
    .Acarreo_de_Salida(add_1_bit_1_acarreo_de_salida));
  Add_1_bit add_1_bit_2 (
    .Acarreo_de_entrada(add_1_bit_1_acarreo_de_salida), .A(A[1]), .B(not_2_out), .Suma(Resultado[1]),
    .Acarreo_de_Salida(add_1_bit_2_acarreo_de_salida));
  Add_1_bit add_1_bit_3 (
    .Acarreo_de_entrada(add_1_bit_2_acarreo_de_salida), .A(A[2]), .B(B[2]), .Suma(Resultado[2]),
    .Acarreo_de_Salida(add_1_bit_3_acarreo_de_salida));
  Add_1_bit add_1_bit_4 (
    .Acarreo_de_entrada(add_1_bit_3_acarreo_de_salida), .A(A[3]), .B(not_3_out), .Suma(Resultado[3]),
    .Acarreo_de_Salida(add_1_bit_4_acarreo_de_salida));
  Add_1_bit add_1_bit_5 (
    .Acarreo_de_entrada(add_1_bit_4_acarreo_de_salida), .A(A[4]), .B(not_4_out), .Suma(Resultado[4]),
    .Acarreo_de_Salida(add_1_bit_5_acarreo_de_salida));
  Add_1_bit add_1_bit_6 (
    .Acarreo_de_entrada(add_1_bit_5_acarreo_de_salida), .A(A[5]), .B(not_5_out), .Suma(Resultado[5]),
    .Acarreo_de_Salida(add_1_bit_6_acarreo_de_salida));
  Add_1_bit add_1_bit_7 (
    .Acarreo_de_entrada(add_1_bit_6_acarreo_de_salida), .A(A[6]), .B(not_6_out), .Suma(Resultado[6]),
    .Acarreo_de_Salida(add_1_bit_7_acarreo_de_salida));
  Add_1_bit add_1_bit_8 (
    .Acarreo_de_entrada(add_1_bit_7_acarreo_de_salida), .A(A[7]), .B(not_7_out), .Suma(Resultado[7]),
    .Acarreo_de_Salida(out_4));
endmodule

module Shift_Register (
  input  in_1,
  input  in_2,
  input  in_3,
  output out_4,
  output out_5,
  output out_6,
  output out_7,
  output out_8,
  output out_9,
  output out_10,
  output out_11,
  output out_12
);

  wire and_1_out, clock_1_out, j_k_ff_1_qn, j_k_ff_2_qn, j_k_ff_3_qn, j_k_ff_4_qn, j_k_ff_5_qn, j_k_ff_6_qn,
       j_k_ff_7_qn, not_1_out;

  Clock clock_1 (.out(clock_1_out));
  not not_1 (not_1_out, in_2);
  and and_1 (and_1_out, in_1, clock_1_out);
  J_K_Flip_Flop j_k_ff_1 (
    .J(in_2), .clk(and_1_out), .K(not_1_out), .Q(out_5), .Qn(j_k_ff_1_qn));  // open: preset, en, reset
  Shift_Register_part shift_register_1 (.clk(in_3));  // open: shift, in, out, load, clr, d0, q0, d1, q1, d2, q2, d3, q3, d4, q4, d5, q5, d6, q6, d7, q7
  J_K_Flip_Flop j_k_ff_2 (
    .J(out_5), .clk(and_1_out), .K(j_k_ff_1_qn), .Q(out_6), .Qn(j_k_ff_2_qn));  // open: preset, en, reset
  J_K_Flip_Flop j_k_ff_3 (
    .J(out_6), .clk(and_1_out), .K(j_k_ff_2_qn), .Q(out_7), .Qn(j_k_ff_3_qn));  // open: preset, en, reset
  J_K_Flip_Flop j_k_ff_4 (
    .J(out_7), .clk(and_1_out), .K(j_k_ff_3_qn), .Q(out_8), .Qn(j_k_ff_4_qn));  // open: preset, en, reset
  J_K_Flip_Flop j_k_ff_5 (
    .J(out_8), .clk(and_1_out), .K(j_k_ff_4_qn), .Q(out_9), .Qn(j_k_ff_5_qn));  // open: preset, en, reset
  J_K_Flip_Flop j_k_ff_6 (
    .J(out_9), .clk(and_1_out), .K(j_k_ff_5_qn), .Q(out_10), .Qn(j_k_ff_6_qn));  // open: preset, en, reset
  J_K_Flip_Flop j_k_ff_7 (
    .J(out_10), .clk(and_1_out), .K(j_k_ff_6_qn), .Q(out_11), .Qn(j_k_ff_7_qn));  // open: preset, en, reset
  J_K_Flip_Flop j_k_ff_8 (.J(out_11), .clk(and_1_out), .K(j_k_ff_7_qn), .Q(out_4));  // open: Qn, preset, en, reset

  assign out_12 = out_4;
endmodule
